// Logisim project 2 бит сумматор.circ as structural Verilog: 1 circuit, main circuit main
module main (
  input  A,
  input  B,
  input  C,
  input  D,
  output F1,
  output F2,
  output F3
);

  wire and_1_out, and_2_out, and_3_out, and_4_out, and_5_out, and_6_out, and_7_out, and_8_out, and_9_out,
       and_10_out, and_11_out;

  and and_1 (and_1_out, A, C);
  and and_2 (and_2_out, B, C, D);
  and and_3 (and_3_out, A, B, D);
  and and_4 (and_4_out, ~A, ~B, C);  // AND_Gate
  and and_5 (and_5_out, ~A, C, ~D);  // AND_Gate
  and and_6 (and_6_out, A, ~B, ~C);  // AND_Gate
  and and_7 (and_7_out, A, ~C, ~D);  // AND_Gate
  and and_8 (and_8_out, ~A, B, ~C, D);  // AND_Gate
  and and_9 (and_9_out, A, B, C, D);
  or or_1 (F2, and_4_out, and_5_out, and_6_out, and_7_out, and_8_out, and_9_out);
  and and_10 (and_10_out, B, ~D);  // AND_Gate
  and and_11 (and_11_out, ~B, D);  // AND_Gate
  or or_2 (F1, and_1_out, and_2_out, and_3_out);
  or or_3 (F3, and_10_out, and_11_out);
endmodule
