// Logisim project Лаба 2 Кузнецов Иван.circ as structural Verilog: 10 circuits, main circuit Инвертор3
module \Полусумматор  (
  input  in_1,
  input  in_2,
  output out_3,
  output out_4
);

  xor xor_1 (out_3, in_1, in_2);
  and and_1 (out_4, in_2, in_1);
endmodule

module \Сумматор  (
  input  in_1,
  input  in_2,
  input  in_3,
  output out_4,
  output out_5
);

  wire \полусумматор_1_out_3 , \полусумматор_1_out_4 , \полусумматор_2_out_4 ;

  \Полусумматор  \u_полусумматор_1  (
    .in_1(in_2), .in_2(in_3), .out_3(\полусумматор_1_out_3 ), .out_4(\полусумматор_1_out_4 ));
  \Полусумматор  \u_полусумматор_2  (
    .in_1(in_1), .in_2(\полусумматор_1_out_3 ), .out_3(out_4), .out_4(\полусумматор_2_out_4 ));
  or or_1 (out_5, \полусумматор_2_out_4 , \полусумматор_1_out_4 );
endmodule

module \Сумматор_8_бит  (
  input  in_1,
  input  [7:0] in_2,
  input  [7:0] in_3,
  output [7:0] out_4,
  output out_5
);

  wire \сумматор_1_out_5 , \сумматор_2_out_5 , \сумматор_3_out_5 , \сумматор_4_out_5 , \сумматор_5_out_5 ,
       \сумматор_6_out_5 , \сумматор_7_out_5 ;

  // Probe on in_2
  // Probe on in_3
  \Сумматор  \u_сумматор_1  (.in_1(in_1), .in_2(in_2[0]), .in_3(in_3[0]), .out_4(out_4[0]), .out_5(\сумматор_1_out_5 ));
  \Сумматор  \u_сумматор_2  (
    .in_1(\сумматор_1_out_5 ), .in_2(in_2[1]), .in_3(in_3[1]), .out_4(out_4[1]), .out_5(\сумматор_2_out_5 ));
  \Сумматор  \u_сумматор_3  (
    .in_1(\сумматор_2_out_5 ), .in_2(in_2[2]), .in_3(in_3[2]), .out_4(out_4[2]), .out_5(\сумматор_3_out_5 ));
  \Сумматор  \u_сумматор_4  (
    .in_1(\сумматор_3_out_5 ), .in_2(in_2[3]), .in_3(in_3[3]), .out_4(out_4[3]), .out_5(\сумматор_4_out_5 ));
  \Сумматор  \u_сумматор_5  (
    .in_1(\сумматор_4_out_5 ), .in_2(in_2[4]), .in_3(in_3[4]), .out_4(out_4[4]), .out_5(\сумматор_5_out_5 ));
  \Сумматор  \u_сумматор_6  (
    .in_1(\сумматор_5_out_5 ), .in_2(in_2[5]), .in_3(in_3[5]), .out_4(out_4[5]), .out_5(\сумматор_6_out_5 ));
  \Сумматор  \u_сумматор_7  (
    .in_1(\сумматор_6_out_5 ), .in_2(in_2[6]), .in_3(in_3[6]), .out_4(out_4[6]), .out_5(\сумматор_7_out_5 ));
  \Сумматор  \u_сумматор_8  (
    .in_1(\сумматор_7_out_5 ), .in_2(in_2[7]), .in_3(in_3[7]), .out_4(out_4[7]), .out_5(out_5));
  // Probe on out_4
endmodule

module \Инвертор3  (
  input  in_1,
  input  [7:0] in_2,
  output [7:0] out_3
);

  // Probe on in_2
  xor xor_1 (out_3[0], in_1, in_2[0]);
  xor xor_2 (out_3[1], in_1, in_2[1]);
  xor xor_3 (out_3[2], in_1, in_2[2]);
  xor xor_4 (out_3[3], in_1, in_2[3]);
  xor xor_5 (out_3[4], in_1, in_2[4]);
  xor xor_6 (out_3[5], in_1, in_2[5]);
  xor xor_7 (out_3[6], in_1, in_2[6]);
  xor xor_8 (out_3[7], in_1, in_2[7]);
  // Probe on out_3
endmodule

module \Вычитатор  (
  input  [7:0] in_1,
  input  [7:0] in_2,
  input  in_3,
  output [7:0] \Вывод ,
  output CO
);

  wire \сумматор_8_бит_1_out_5 ;
  wire [7:0] \инвертор3_1_out_3 ;

  // Probe on in_2
  // Probe on in_1
  \Инвертор3  \u_инвертор3_1  (.in_1(in_3), .in_2(in_2), .out_3(\инвертор3_1_out_3 ));
  \Сумматор_8_бит  \u_сумматор_8_бит_1  (
    .in_1(in_3), .in_2(in_1), .in_3(\инвертор3_1_out_3 ), .out_5(\сумматор_8_бит_1_out_5 ), .out_4(\Вывод ));
  xor xor_1 (CO, \сумматор_8_бит_1_out_5 , in_3);
  // Probe on \Вывод 

  // Notes on the sheet:
  //   A
  //   B
  //   +/-
  //   SUM
endmodule

module \_4_Бита_суматор  (
  input  in_1,
  input  [3:0] in_2,
  input  [3:0] in_3,
  output [3:0] out_4,
  output out_5
);

  wire \сумматор_1_out_5 , \сумматор_2_out_5 , \сумматор_3_out_5 ;

  // Probe on in_2
  // Probe on in_3
  \Сумматор  \u_сумматор_1  (.in_1(in_1), .in_2(in_2[0]), .in_3(in_3[0]), .out_4(out_4[0]), .out_5(\сумматор_1_out_5 ));
  \Сумматор  \u_сумматор_2  (
    .in_1(\сумматор_1_out_5 ), .in_2(in_2[1]), .in_3(in_3[1]), .out_4(out_4[1]), .out_5(\сумматор_2_out_5 ));
  \Сумматор  \u_сумматор_3  (
    .in_1(\сумматор_2_out_5 ), .in_2(in_2[2]), .in_3(in_3[2]), .out_4(out_4[2]), .out_5(\сумматор_3_out_5 ));
  \Сумматор  \u_сумматор_4  (
    .in_1(\сумматор_3_out_5 ), .in_2(in_2[3]), .in_3(in_3[3]), .out_4(out_4[3]), .out_5(out_5));
  // Probe on out_4
endmodule

module \Умножатор5  (
  input  [3:0] in_1,
  input  [3:0] in_2,
  output [7:0] out_3
);

  wire [2:0] and_2_out;
  wire [3:0] and_5_out, and_8_out, and_13_out;
  wire [3:1] \n4_бита_суматор_1_out_4 , \n4_бита_суматор_2_out_4 ;
  wire [3:3] \n4_бита_суматор_1_out_5 , \n4_бита_суматор_2_out_5 ;

  // Probe on in_2
  // Probe on in_1
  and and_1 (out_3[0], in_2[0], in_1[0]);
  and and_2 (and_2_out[0], in_2[0], in_1[1]);
  and and_3 (and_2_out[2], in_2[0], in_1[3]);
  and and_4 (and_2_out[1], in_2[0], in_1[2]);
  \_4_Бита_суматор  \u_4_бита_суматор_1  (
    .in_2(and_5_out), .in_3({1'b0, and_2_out}), .in_1(1'b0), .out_4({\n4_бита_суматор_1_out_4 , out_3[1]}),
    .out_5(\n4_бита_суматор_1_out_5 [3]));
  and and_5 (and_5_out[0], in_2[1], in_1[0]);
  and and_6 (and_5_out[1], in_2[1], in_1[1]);
  and and_7 (and_5_out[2], in_2[1], in_1[2]);
  and and_8 (and_8_out[0], in_2[2], in_1[0]);
  and and_9 (and_5_out[3], in_2[1], in_1[3]);
  \_4_Бита_суматор  \u_4_бита_суматор_2  (
    .in_2(and_8_out), .in_3({\n4_бита_суматор_1_out_5 [3], \n4_бита_суматор_1_out_4 }), .in_1(1'b0),
    .out_4({\n4_бита_суматор_2_out_4 , out_3[2]}), .out_5(\n4_бита_суматор_2_out_5 [3]));
  // Probe on out_3
  and and_10 (and_8_out[1], in_2[2], in_1[1]);
  and and_11 (and_8_out[2], in_2[2], in_1[2]);
  and and_12 (and_8_out[3], in_2[2], in_1[3]);
  and and_13 (and_13_out[0], in_2[3], in_1[0]);
  and and_14 (and_13_out[1], in_2[3], in_1[1]);
  and and_15 (and_13_out[2], in_2[3], in_1[2]);
  and and_16 (and_13_out[3], in_2[3], in_1[3]);
  \_4_Бита_суматор  \u_4_бита_суматор_3  (
    .in_2(and_13_out), .in_3({\n4_бита_суматор_2_out_5 [3], \n4_бита_суматор_2_out_4 }), .in_1(1'b0),
    .out_4(out_3[6:3]), .out_5(out_3[7]));
endmodule

module \Лог_сдвиг  (
  input  [7:0] in_1,
  input  in_2,
  output [7:0] out_3
);

  wire and_1_out, and_3_out, and_4_out, and_5_out, and_6_out, and_7_out, and_8_out, and_9_out, and_10_out,
       and_11_out, and_12_out, and_14_out, not_1_out;

  not not_1 (not_1_out, in_2);
  and and_1 (and_1_out, in_1[0], not_1_out);
  and and_2 (out_3[0], in_2, in_1[1]);
  and and_3 (and_3_out, in_1[1], not_1_out);
  and and_4 (and_4_out, in_2, in_1[2]);
  and and_5 (and_5_out, in_1[2], not_1_out);
  and and_6 (and_6_out, in_2, in_1[3]);
  and and_7 (and_7_out, in_1[3], not_1_out);
  and and_8 (and_8_out, in_2, in_1[4]);
  and and_9 (and_9_out, in_1[4], not_1_out);
  and and_10 (and_10_out, in_2, in_1[5]);
  and and_11 (and_11_out, in_1[5], not_1_out);
  and and_12 (and_12_out, in_2, in_1[6]);
  and and_13 (out_3[7], in_1[6], not_1_out);
  and and_14 (and_14_out, in_2, in_1[7]);
  or or_1 (out_3[1], and_1_out, and_4_out);
  or or_2 (out_3[2], and_3_out, and_6_out);
  or or_3 (out_3[3], and_5_out, and_8_out);
  or or_4 (out_3[4], and_7_out, and_10_out);
  or or_5 (out_3[5], and_9_out, and_12_out);
  or or_6 (out_3[6], and_11_out, and_14_out);
endmodule

module \Арифм_сдвиг  (
  input  [7:0] in_1,
  input  in_2,
  output [7:0] out_3
);

  wire and_1_out, and_3_out, and_4_out, and_5_out, and_6_out, and_7_out, and_8_out, and_9_out, and_10_out,
       and_11_out, and_12_out, and_14_out, not_1_out;

  not not_1 (not_1_out, in_2);
  and and_1 (and_1_out, in_2, in_1[0]);
  and and_2 (out_3[0], in_1[0], not_1_out);
  and and_3 (and_3_out, in_1[1], not_1_out);
  and and_4 (and_4_out, in_2, in_1[2]);
  and and_5 (and_5_out, in_1[2], not_1_out);
  and and_6 (and_6_out, in_2, in_1[3]);
  and and_7 (and_7_out, in_1[3], not_1_out);
  and and_8 (and_8_out, in_2, in_1[4]);
  and and_9 (and_9_out, in_1[4], not_1_out);
  and and_10 (and_10_out, in_2, in_1[5]);
  and and_11 (and_11_out, in_1[5], not_1_out);
  and and_12 (and_12_out, in_2, in_1[6]);
  and and_13 (out_3[7], in_2, in_1[7]);
  and and_14 (and_14_out, in_1[7], not_1_out);
  or or_1 (out_3[1], and_1_out, and_4_out);
  or or_2 (out_3[2], and_3_out, and_6_out);
  or or_3 (out_3[3], and_5_out, and_8_out);
  or or_4 (out_3[4], and_7_out, and_10_out);
  or or_5 (out_3[5], and_9_out, and_12_out);
  or or_6 (out_3[6], and_11_out, and_14_out);
endmodule

module \Цикл_сдвиг  (
  input  [7:0] in_1,
  input  in_2,
  output [7:0] out_3
);

  wire and_1_out, and_2_out, and_3_out, and_4_out, and_5_out, and_6_out, and_7_out, and_8_out, and_9_out,
       and_10_out, and_11_out, and_12_out, and_13_out, and_14_out, and_15_out, and_16_out, not_1_out;

  not not_1 (not_1_out, in_2);
  and and_1 (and_1_out, in_2, in_1[0]);
  and and_2 (and_2_out, in_1[0], not_1_out);
  and and_3 (and_3_out, in_2, in_1[1]);
  and and_4 (and_4_out, in_1[1], not_1_out);
  and and_5 (and_5_out, in_2, in_1[2]);
  and and_6 (and_6_out, in_1[2], in_2);
  and and_7 (and_7_out, not_1_out, in_1[3]);
  and and_8 (and_8_out, in_1[3], in_2);
  and and_9 (and_9_out, in_2, in_1[4]);
  and and_10 (and_10_out, in_1[4], in_2);
  and and_11 (and_11_out, not_1_out, in_1[5]);
  and and_12 (and_12_out, in_1[5], in_2);
  and and_13 (and_13_out, in_2, in_1[6]);
  and and_14 (and_14_out, in_1[6], not_1_out);
  and and_15 (and_15_out, in_2, in_1[7]);
  and and_16 (and_16_out, in_1[7], not_1_out);
  or or_1 (out_3[0], and_16_out, and_3_out);
  or or_2 (out_3[1], and_2_out, and_5_out);
  or or_3 (out_3[2], and_4_out, and_7_out);
  or or_4 (out_3[3], and_6_out, and_9_out);
  or or_5 (out_3[4], and_8_out, and_11_out);
  or or_6 (out_3[5], and_10_out, and_13_out);
  or or_7 (out_3[6], and_12_out, and_15_out);
  or or_8 (out_3[7], and_14_out, and_1_out);
endmodule
