// Logisim project Шифратор.circ as structural Verilog: 3 circuits, main circuit main
module main (
  input  _0,
  input  _1,
  input  _2,
  input  _3,
  input  _4,
  input  _5,
  input  _6,
  input  _7,
  input  _8,
  input  _9,
  input  _10,
  input  _11,
  input  _12,
  input  _13,
  input  _14,
  input  _15,
  output [3:0] out_17,
  output \ошибка 
);

  wire or_1_out, or_2_out, or_3_out, or_4_out;

  or or_1 (or_1_out, _15, _14, _13, _12, _11, _10, _9, _8);
  or or_2 (or_2_out, _15, _14, _13, _12, _7, _6, _5, _4);
  or or_3 (or_3_out, _15, _14, _11, _10, _7, _6, _3, _2);
  or or_4 (or_4_out, _7, _11, _15, _13, _9, _5, _3, _1);
  NotExactlyOne xnor_1 (
    .out(\ошибка ), .in0(_15), .in1(_14), .in2(_13), .in3(_12), .in4(_11), .in5(_10), .in6(_9), .in7(_8),
    .in8(_7), .in9(_6), .in10(_5), .in11(_4), .in12(_3), .in13(_2), .in14(_1), .in15(_0));
  ExactlyOne xor_1 (.out(out_17[3]), .in0(or_1_out), .in1(\ошибка ), .in2(\ошибка ));
  ExactlyOne xor_2 (.out(out_17[2]), .in0(or_2_out), .in1(\ошибка ), .in2(\ошибка ));
  ExactlyOne xor_3 (.out(out_17[1]), .in0(or_3_out), .in1(\ошибка ), .in2(\ошибка ));
  ExactlyOne xor_4 (.out(out_17[0]), .in0(or_4_out), .in1(\ошибка ), .in2(\ошибка ));
endmodule

module \Дешифратор  (
  input  _0,
  input  _1,
  input  _2,
  input  _3,
  input  _4,
  input  _5,
  input  _6,
  input  _7,
  input  _8,
  input  _9,
  input  A,
  input  B,
  input  C,
  input  D,
  input  E,
  input  F,
  output [3:0] out_17,
  output \ошибка 
);

  wire and_1_out, and_2_out, and_3_out, and_4_out, and_5_out, and_6_out, and_7_out, and_8_out, and_9_out,
       and_10_out, and_11_out, and_12_out, and_13_out, and_14_out, and_15_out, not_1_out, not_2_out,
       not_3_out, not_4_out, not_5_out, not_6_out, not_7_out, not_8_out, not_9_out, not_10_out, not_11_out,
       not_12_out, not_13_out, not_14_out, not_15_out, not_16_out, not_17_out, not_18_out, not_19_out,
       not_20_out, not_21_out, not_22_out, not_23_out, not_24_out, not_25_out, not_26_out, not_27_out,
       not_28_out, or_1_out, or_2_out, or_3_out, or_4_out;

  or or_1 (or_1_out, F, E, D, C, B, A, _9, _8);
  or or_2 (or_2_out, F, E, D, C, _7, _6, _5, _4);
  or or_3 (or_3_out, F, E, B, A, _7, _6, _3, _2);
  or or_4 (or_4_out, _7, B, F, D, _9, _5, _3, _1);
  ExactlyOne xor_1 (.out(out_17[3]), .in0(or_1_out), .in1(\ошибка ), .in2(\ошибка ));
  ExactlyOne xor_2 (.out(out_17[2]), .in0(or_2_out), .in1(\ошибка ), .in2(\ошибка ));
  ExactlyOne xor_3 (.out(out_17[1]), .in0(or_3_out), .in1(\ошибка ), .in2(\ошибка ));
  ExactlyOne xor_4 (.out(out_17[0]), .in0(or_4_out), .in1(\ошибка ), .in2(\ошибка ));
  NotExactlyOne xnor_1 (
    .out(\ошибка ), .in0(F), .in1(E), .in2(D), .in3(C), .in4(B), .in5(A), .in6(_9), .in7(_8), .in8(_7),
    .in9(_6), .in10(_5), .in11(_4), .in12(_3), .in13(_2), .in14(_1), .in15(_0));
  not not_1 (not_1_out, out_17[3]);
  not not_2 (not_2_out, out_17[2]);
  not not_3 (not_3_out, out_17[1]);
  not not_4 (not_4_out, out_17[3]);
  not not_5 (not_5_out, out_17[2]);
  not not_6 (not_6_out, out_17[0]);
  not not_7 (not_7_out, out_17[3]);
  not not_8 (not_8_out, out_17[2]);
  not not_9 (not_9_out, out_17[3]);
  not not_10 (not_10_out, out_17[1]);
  not not_11 (not_11_out, out_17[0]);
  not not_12 (not_12_out, out_17[3]);
  not not_13 (not_13_out, out_17[1]);
  not not_14 (not_14_out, out_17[3]);
  not not_15 (not_15_out, out_17[0]);
  not not_16 (not_16_out, out_17[3]);
  not not_17 (not_17_out, out_17[2]);
  not not_18 (not_18_out, out_17[1]);
  not not_19 (not_19_out, out_17[0]);
  not not_20 (not_20_out, out_17[2]);
  not not_21 (not_21_out, out_17[1]);
  not not_22 (not_22_out, out_17[2]);
  not not_23 (not_23_out, out_17[0]);
  not not_24 (not_24_out, out_17[2]);
  not not_25 (not_25_out, out_17[1]);
  not not_26 (not_26_out, out_17[0]);
  not not_27 (not_27_out, out_17[1]);
  not not_28 (not_28_out, out_17[0]);
  and and_1 (and_1_out, not_1_out, not_2_out, not_3_out, out_17[0]);
  // Probe on and_1_out
  // Probe on and_2_out
  and and_2 (and_2_out, not_4_out, not_5_out, out_17[1], not_6_out);
  and and_3 (and_3_out, not_7_out, not_8_out, out_17[1], out_17[0]);
  // Probe on and_3_out
  and and_4 (and_4_out, not_9_out, out_17[2], not_10_out, not_11_out);
  // Probe on and_4_out
  // Probe on and_5_out
  and and_5 (and_5_out, not_12_out, out_17[2], not_13_out, out_17[0]);
  // Probe on and_6_out
  and and_6 (and_6_out, not_14_out, out_17[2], out_17[1], not_15_out);
  and and_7 (and_7_out, not_16_out, out_17[2], out_17[1], out_17[0]);
  // Probe on and_7_out
  and and_8 (and_8_out, out_17[3], not_17_out, not_18_out, not_19_out);
  // Probe on and_8_out
  and and_9 (and_9_out, out_17[3], not_20_out, not_21_out, out_17[0]);
  // Probe on and_9_out
  and and_10 (and_10_out, out_17[3], not_22_out, out_17[1], not_23_out);
  // Probe on and_10_out
  and and_11 (and_11_out, out_17[3], not_24_out, out_17[1], out_17[0]);
  // Probe on and_11_out
  // Probe on and_12_out
  and and_12 (and_12_out, out_17[3], out_17[2], not_25_out, not_26_out);
  // Probe on and_13_out
  and and_13 (and_13_out, out_17[3], out_17[2], not_27_out, out_17[0]);
  // Probe on and_14_out
  and and_14 (and_14_out, out_17[3], out_17[2], out_17[1], not_28_out);
  // Probe on and_15_out
  and and_15 (and_15_out, out_17[3], out_17[2], out_17[1], out_17[0]);
endmodule

module \мультиплексор  (
  input  in_1,
  input  in_2,
  input  in_3,
  input  in_4,
  input  in_5,
  input  in_6,
  input  in_7,
  input  in_8,
  input  in_9,
  input  in_10,
  input  in_11
);

  wire and_1_out, and_2_out, and_3_out, and_4_out, and_5_out, and_6_out, and_7_out, and_8_out, not_1_out,
       not_2_out, not_3_out, or_1_out;

  not not_1 (not_1_out, in_9);
  not not_2 (not_2_out, in_10);
  not not_3 (not_3_out, in_11);
  and and_1 (and_1_out, not_1_out, not_2_out, not_3_out, in_1);
  and and_2 (and_2_out, in_11, in_2, not_1_out, not_2_out);
  and and_3 (and_3_out, not_3_out, in_3, in_10, not_1_out);
  and and_4 (and_4_out, in_4, not_1_out, in_10, in_11);
  and and_5 (and_5_out, in_9, in_5, not_3_out, not_2_out);
  and and_6 (and_6_out, in_11, not_2_out, in_6, in_9);
  and and_7 (and_7_out, in_9, not_3_out, in_7, in_10);
  and and_8 (and_8_out, in_11, in_8, in_9, in_10);
  or or_1 (or_1_out, and_1_out, and_2_out, and_3_out, and_4_out, and_5_out, and_6_out, and_7_out, and_8_out);
  // Probe on or_1_out
endmodule
