// Logisim project 1ИЛИ.circ as structural Verilog: 1 circuit, main circuit main
module main (
  input  in_1,
  input  in_2,
  output out_3
);

  wire transistor_4_out;

  Transistor #(.\type ("n")) transistor_1 (.in(1'b1), .out(out_3), .gate(in_1));
  Transistor #(.\type ("n")) transistor_2 (.in(1'b1), .out(out_3), .gate(in_2));
  Transistor transistor_3 (.in(transistor_4_out), .out(out_3), .gate(in_1));
  Transistor transistor_4 (.in(1'b0), .out(transistor_4_out), .gate(in_2));
endmodule
